// Logisim project evolution_D_FF.circ as structural Verilog
module flipflop (
  input  preset,
  input  data,
  input  clk,
  input  clear,
  output Q
);

  wire latch_1_q, latch_2_qb, not_1_out;

  not not_1 (not_1_out, clk);
  latch latch_1 (.preset(preset), .data(data), .enable(not_1_out), .clear(clear), .Q(latch_1_q));  // open: Qb
  latch latch_2 (.preset(preset), .data(latch_1_q), .enable(clk), .clear(clear), .Q(Q), .Qb(latch_2_qb));
endmodule

module latch (
  input  preset,
  input  data,
  input  enable,
  input  clear,
  output Q,
  output Qb
);

  wire A_out, B_out, C_out, D_out, E_out;

  not E (E_out, data);
  not A (A_out, preset);
  nand C (C_out, data, enable);
  nand D (D_out, enable, E_out);
  not B (B_out, clear);
  nand nand_1 (Q, C_out, A_out, Qb);
  nand nand_2 (Qb, Q, B_out, D_out);
endmodule
